// Logisim project Build-a-comp modules.circ as structural Verilog: 14 circuits, main circuit Tests
module Tests (
);

  RAM ram_1 ();  // open: Address_in_A___Lowest_Bits, Address_in_B, Address_in_C, Address_in_D___Highest_Bits, Data_in_A___Low_bits, Data_in_B___High_bits, Control_In, Control_Out, Data_out_A___Low_bits, Data_out_B___High_bits, out_9, out_10, out_11, out_12, out_13, out_14, out_15, out_16, Write, Enable_Write, out_21
endmodule

module Arithmetic_Unit (
  input  [3:0] Control_In,
  input  [3:0] Input_A,
  input  [3:0] Input_B,
  output Add___Zero,
  output [3:0] Bool_Test_Result,
  output Pass___Zero,
  output Sub___Eq,
  output out_8,
  output Sub___Neg,
  output [3:0] Result,
  output [3:0] Control_Out,
  output out_12,
  output out_13,
  output out_14,
  output out_15
);

  wire and_1_out, comparator_1_eq, comparator_1_lt, comparator_2_gt, multiplexer_2_out;
  wire [3:0] multiplexer_1_out, not_1_out;

  or or_1 (Control_Out[3], Control_In[3], comparator_2_gt);
  Multiplexer #(.select(2), .width(4), .disabled(0), .enable("false")) multiplexer_1 (
    .in0(Input_B), .in1(4'b0000), .in2(not_1_out), .in3(not_1_out), .out(multiplexer_1_out),
    .sel(Control_In[1:0]));
  assign not_1_out = ~Input_B;  // NOT_Gate not_1, 4 bits wide
  Demultiplexer_part #(.select(2), .enable("false")) demultiplexer_1 (
    .out0(Add___Zero), .out1(Pass___Zero), .out2(Sub___Eq), .out3(Sub___Neg), .in(1'b1), .sel(Control_In[1:0]));
  Multiplexer #(.select(2), .disabled(0), .enable("false")) multiplexer_2 (
    .in0(Control_In[2]), .in1(1'b0), .in2(Control_In[2]), .in3(Control_In[2]), .out(multiplexer_2_out),
    .sel(Control_In[1:0]));
  Adder #(.width(4)) adder_1 (
    .a(Input_A), .b(multiplexer_1_out), .out({out_12, out_13, out_14, out_15}), .cin(multiplexer_2_out),
    .cout(Control_Out[2]));
  Comparator #(.width(4)) comparator_1 (
    .a({out_12, out_13, out_14, out_15}), .b(4'b0000), .eq(comparator_1_eq), .lt(comparator_1_lt));  // open: gt
  Comparator #(.width(4), .mode("unsigned")) comparator_2 (
    .a({out_12, out_13, out_14, out_15}), .b(4'b0000), .gt(comparator_2_gt));  // open: eq, lt
  and and_1 (and_1_out, ~Control_In[3], comparator_1_eq);  // AND_Gate
  Multiplexer #(.select(2), .disabled(0), .enable("false")) multiplexer_3 (
    .in0(and_1_out), .in1(and_1_out), .in2(and_1_out), .in3(comparator_1_lt), .out(Bool_Test_Result[3]),
    .sel(Control_In[1:0]));

  assign Bool_Test_Result[2:0] = {3{Bool_Test_Result[3]}};
  assign Control_Out[1:0] = Control_In[1:0];
  assign out_8 = Bool_Test_Result[3];
  assign Result = {out_12, out_13, out_14, out_15};

  // Notes on the sheet:
  //   Input_A: pull=down
  //   Control_In: pull=down
  //   Control_Out: pull=down
  //   Input_B: pull=down
endmodule

module Clock (
  input  Manual,
  input  Reset,
  output Phi_1,
  output [3:0] Phase_1,
  output Phi_2,
  output [3:0] Phase_2
);

  wire clock_1_out, xor_1_out;
  wire [1:0] counter_1_q;

  Clock_part clock_1 (.out(clock_1_out));
  xor xor_1 (xor_1_out, clock_1_out, Manual);
  Demultiplexer_part #(.select(2), .disabled(0), .enable("false")) demultiplexer_1 (
    .out1(Phase_1[0]), .out3(Phase_2[0]), .in(1'b1), .sel(counter_1_q));  // open: out0, out2
  Counter #(.width(2), .max('h3)) counter_1 (
    .Q(counter_1_q), .clk(xor_1_out), .clr(Reset));  // open: load, D, count, carry

  assign Phase_1[1] = Reset;
  assign Phase_2[1] = Reset;
  assign Phi_1 = Phase_1[0];
  assign Phi_2 = Phase_2[0];

  // Notes on the sheet:
  //   Manual: pull=down
  //   Reset: pull=down
endmodule

module Demultiplexer (
  input  [3:0] Control_In,
  input  [3:0] Input,
  output [3:0] Output_A,
  output [3:0] Output_B,
  output [3:0] Output_C,
  output [3:0] Output_D,
  output [3:0] Control_Out,
  output out_8,
  output out_9,
  output out_10,
  output out_11,
  output out_12,
  output out_13,
  output out_14,
  output out_15
);

  wire [1:0] bit_extender_1_out;

  Bit_Extender #(.in_width(4), .out_width(2)) bit_extender_1 (.in(Control_In), .out(bit_extender_1_out));
  Demultiplexer_part #(.select(2), .width(4), .disabled(0), .enable("false")) demultiplexer_1 (
    .out0(Output_A), .out1(Output_B), .out2(Output_C), .out3(Output_D), .in(Input), .sel(bit_extender_1_out));
  Demultiplexer_part #(.select(2), .disabled(0), .enable("false")) demultiplexer_2 (
    .out0(out_14), .out1(out_12), .out2(out_15), .out3(out_13), .in(1'b1), .sel(bit_extender_1_out));

  assign Control_Out = Control_In;
  assign out_8 = Input[3];
  assign out_9 = Input[2];
  assign out_10 = Input[1];
  assign out_11 = Input[0];

  // Notes on the sheet:
  //   Control_In: pull=down
  //   Input: pull=down
endmodule

module Fanout (
  input  [3:0] Input,
  output [3:0] Output_A,
  output [3:0] Output_B,
  output [3:0] Output_C,
  output [3:0] Output_D,
  output out_6,
  output out_7,
  output out_8,
  output out_9
);


  assign out_6 = Input[3];
  assign out_7 = Input[2];
  assign out_8 = Input[1];
  assign out_9 = Input[0];
  assign Output_A = Input;
  assign Output_B = Input;
  assign Output_C = Input;
  assign Output_D = Input;

  // Notes on the sheet:
  //   Input: pull=down
endmodule

module Left_Shift (
  input  [3:0] Chain_In,
  input  [3:0] Data_In,
  input  [3:0] Control_In,
  output out_4,
  output out_5,
  output out_6,
  output out_7,
  output [3:0] Data_Out,
  output [3:0] Control_Out,
  output [3:0] Chain_Out
);

  wire [1:0] bit_extender_1_out;
  wire [2:0] multiplexer_1_out;
  wire [9:0] shifter_1_out;

  Pull_Resistor pull_resistor_1 (.node(Control_In[1]));
  Pull_Resistor pull_resistor_2 (.node(Control_In[3]));
  Pull_Resistor pull_resistor_3 (.node(Control_In[2]));
  Pull_Resistor #(.pull(1)) pull_resistor_4 (.node(Control_In[0]));
  Multiplexer #(.select(2), .width(3), .disabled(0), .enable("false")) multiplexer_1 (
    .in0(3'b000), .in1({Chain_In[0], 2'b00}), .in2({Chain_In[1], Chain_In[2], 1'b0}),
    .in3({Chain_In[0], Chain_In[1], Chain_In[2]}), .out(multiplexer_1_out), .sel(bit_extender_1_out));
  Bit_Extender #(.in_width(4), .out_width(2)) bit_extender_1 (.in(Control_In), .out(bit_extender_1_out));
  Shifter #(.width(10)) shifter_1 (
    .in({3'b000, Data_In, multiplexer_1_out}), .\dist (Control_In),
    .out({shifter_1_out[9:7], Data_Out, shifter_1_out[2:0]}));
  Multiplexer #(.select(2), .width(4), .disabled(0), .enable("false")) multiplexer_2 (
    .in0({1'b0, Data_Out[2], {2{Data_Out[3]}}}), .in1({1'b0, Data_Out[2], Data_Out[3], shifter_1_out[7]}),
    .in2({1'b0, shifter_1_out[7], {2{shifter_1_out[8]}}}),
    .in3({1'b0, shifter_1_out[7], shifter_1_out[8], shifter_1_out[9]}), .out(Chain_Out),
    .sel(bit_extender_1_out));

  assign Control_Out = Control_In;
  assign out_4 = Data_Out[3];
  assign out_5 = Data_Out[2];
  assign out_6 = Data_Out[1];
  assign out_7 = Data_Out[0];

  // Notes on the sheet:
  //   Data_In: pull=down
  //   Chain_In: pull=down
endmodule

module Logic_Unit (
  input  [3:0] Onput_A,
  input  [3:0] Onput_B,
  input  [3:0] Control_In,
  output [3:0] Result,
  output out_5,
  output out_6,
  output out_7,
  output out_8,
  output [3:0] Control_Out,
  output NOT,
  output AND,
  output OR,
  output XOR
);

  wire [1:0] bit_extender_1_out;
  wire [3:0] and_1_out, not_1_out, or_1_out, xor_1_out;

  assign not_1_out = ~Onput_A;  // NOT_Gate not_1, 4 bits wide
  assign and_1_out = Onput_A & Onput_B;  // AND_Gate and_1, 4 bits wide
  assign or_1_out = Onput_A | Onput_B;  // OR_Gate or_1, 4 bits wide
  assign xor_1_out = Onput_A ^ Onput_B;  // XOR_Gate xor_1, 4 bits wide
  Bit_Extender #(.in_width(4), .out_width(2)) bit_extender_1 (.in(Control_In), .out(bit_extender_1_out));
  Multiplexer #(.select(2), .width(4), .disabled(0), .enable("false")) multiplexer_1 (
    .in0(not_1_out), .in1(and_1_out), .in2(or_1_out), .in3(xor_1_out), .out({out_5, out_6, out_7, out_8}),
    .sel(bit_extender_1_out));
  Demultiplexer_part #(.select(2), .disabled(0), .enable("false")) demultiplexer_1 (
    .out0(NOT), .out1(AND), .out2(OR), .out3(XOR), .in(1'b1), .sel(bit_extender_1_out));

  assign Control_Out = Control_In;
  assign Result = {out_5, out_6, out_7, out_8};

  // Notes on the sheet:
  //   Onput_B: pull=down
  //   Onput_A: pull=down
  //   Control_In: pull=down
endmodule

module Merger (
  input  [3:0] Port_a___xxba,
  input  [3:0] Port_b___xxxb,
  input  [3:0] Port_c___xxdc,
  input  [3:0] Port_d___xxxd,
  output [3:0] _4_Bit_Port_A___dcba,
  output [3:0] _2_Bit_Port_B___xxdc
);


  assign _2_Bit_Port_B___xxdc[1:0] = Port_c___xxdc[1:0];
  assign _4_Bit_Port_A___dcba = {Port_c___xxdc[1:0], Port_a___xxba[1:0]};
  assign Port_b___xxxb[0] = Port_a___xxba[1];
  assign Port_d___xxxd[0] = Port_c___xxdc[1];
endmodule

module Multiplexor (
  input  [3:0] Select_In,
  input  [3:0] Input_A,
  input  [3:0] Input_B,
  input  [3:0] Input_C,
  input  [3:0] Input_D,
  output [3:0] Output,
  output out_7,
  output out_8,
  output out_9,
  output out_10,
  output [3:0] Select_Out,
  output out_12,
  output out_13,
  output out_14,
  output out_15
);

  wire [1:0] bit_extender_1_out;

  Bit_Extender #(.in_width(4), .out_width(2)) bit_extender_1 (.in(Select_In), .out(bit_extender_1_out));
  Multiplexer #(.select(2), .width(4), .disabled(0), .enable("false")) multiplexer_1 (
    .in0(Input_A), .in1(Input_B), .in2(Input_C), .in3(Input_D), .out({out_7, out_8, out_9, out_10}),
    .sel(bit_extender_1_out));
  Demultiplexer_part #(.select(2), .disabled(0), .enable("false")) demultiplexer_1 (
    .out0(out_14), .out1(out_12), .out2(out_15), .out3(out_13), .in(1'b1), .sel(bit_extender_1_out));

  assign Output = {out_7, out_8, out_9, out_10};
  assign Select_Out = Select_In;

  // Notes on the sheet:
  //   Input_D: pull=down
  //   Input_C: pull=down
  //   Input_A: pull=down
  //   Input_B: pull=down
  //   Select_In: pull=down
endmodule

module OR (
  input  [3:0] Chain,
  input  [3:0] Input_A,
  input  [3:0] Input_B,
  input  [3:0] Input_C,
  input  [3:0] Input_D,
  output [3:0] Output_A,
  output [3:0] Output,
  output [3:0] Output_C,
  output [3:0] Output_D,
  output out_10,
  output [3:0] out_11
);

  wire [3:1] or_1_out;

  assign {or_1_out, out_10} = Chain | Input_D | Input_C | Input_B | Input_A;  // OR_Gate or_1, 4 bits wide

  assign out_11[0] = out_10;
  assign Output = Input_B;
  assign Output_A = Input_A;
  assign Output_C = Input_C;
  assign Output_D = Input_D;

  // Notes on the sheet:
  //   Input_D: pull=down
  //   Input_A: pull=down
  //   Input_C: pull=down
  //   Chain: pull=down
  //   Input_B: pull=down
endmodule

module RAM (
  input  [3:0] Address_in_A___Lowest_Bits,
  input  [3:0] Address_in_B,
  input  [3:0] Address_in_C,
  input  [3:0] Address_in_D___Highest_Bits,
  input  [3:0] Data_in_A___Low_bits,
  input  [3:0] Data_in_B___High_bits,
  input  [3:0] Control_In,
  input  Enable_Write,
  output out_9,
  output out_10,
  output out_11,
  output out_12,
  output out_13,
  output out_14,
  output out_15,
  output out_16,
  output [3:0] Data_out_A___Low_bits,
  output [3:0] Data_out_B___High_bits,
  output Write,
  output [3:0] Control_Out,
  output out_21
);

  wire not_1_out;

  and and_1 (Write, Control_In[2], Enable_Write);
  not not_1 (not_1_out, Write);
  RAM_part #(.addrWidth(16), .bus("separate")) ram_1 (
    .addr({Address_in_D___Highest_Bits, Address_in_C, Address_in_B, Address_in_A___Lowest_Bits}),
    .din({Data_in_B___High_bits, Data_in_A___Low_bits}),
    .data({Data_out_B___High_bits, Data_out_A___Low_bits}), .str(Write), .clk(Control_In[0]), .ld(not_1_out));  // open: sel, clr
  Pull_Resistor pull_resistor_1 (.node(Data_out_B___High_bits[3]));
  Pull_Resistor pull_resistor_2 (.node(Data_out_B___High_bits[2]));
  Pull_Resistor pull_resistor_3 (.node(Data_out_B___High_bits[1]));
  Pull_Resistor pull_resistor_4 (.node(Data_out_A___Low_bits[3]));
  Pull_Resistor pull_resistor_5 (.node(Data_out_B___High_bits[0]));
  Pull_Resistor pull_resistor_6 (.node(Data_out_A___Low_bits[0]));
  Pull_Resistor pull_resistor_7 (.node(Data_out_A___Low_bits[1]));
  Pull_Resistor pull_resistor_8 (.node(Data_out_A___Low_bits[2]));

  assign Control_Out = Control_In;
  assign out_9 = Data_out_B___High_bits[3];
  assign out_10 = Data_out_B___High_bits[2];
  assign out_11 = Data_out_B___High_bits[1];
  assign out_12 = Data_out_B___High_bits[0];
  assign out_13 = Data_out_A___Low_bits[3];
  assign out_14 = Data_out_A___Low_bits[2];
  assign out_15 = Data_out_A___Low_bits[1];
  assign out_16 = Data_out_A___Low_bits[0];
  assign out_21 = 1'b1;

  // Notes on the sheet:
  //   Data_out_B___High_bits: pull=down
  //   Address_in_D___Highest_Bits: pull=down
  //   Address_in_A___Lowest_Bits: pull=down
  //   Control_In: pull=down
  //   Data_in_A___Low_bits: pull=down
  //   Data_out_A___Low_bits: pull=down
  //   Address_in_C: pull=down
  //   Address_in_B: pull=down
  //   Enable_Write: pull=down
  //   Data_in_B___High_bits: pull=down
endmodule

module Register (
  input  [3:0] Data_In,
  input  [3:0] Control_In,
  output [3:0] Data_Out,
  output out_4,
  output out_5,
  output out_6,
  output out_7,
  output [3:0] Control_Out
);

  Pull_Resistor pull_resistor_1 (.node(Control_In[1]));
  Pull_Resistor #(.pull(1)) pull_resistor_2 (.node(Control_In[0]));
  Pull_Resistor #(.pull(1)) pull_resistor_3 (.node(Control_In[2]));
  Pull_Resistor pull_resistor_4 (.node(Control_In[3]));
  Register_part #(.width(4), .trigger("high")) register_1 (
    .D(Data_In), .en(Control_In[2]), .Q(Data_Out), .clk(Control_In[0]), .clr(Control_In[1]));

  assign Control_Out = Control_In;
  assign out_4 = Data_Out[3];
  assign out_5 = Data_Out[2];
  assign out_6 = Data_Out[1];
  assign out_7 = Data_Out[0];

  // Notes on the sheet:
  //   Data_In: pull=down
endmodule

module Right_Shift (
  input  [3:0] Chain_In,
  input  [3:0] Data_In,
  input  [3:0] Control_In,
  output out_4,
  output out_5,
  output out_6,
  output out_7,
  output [3:0] Data_Out,
  output [3:0] Control_Out,
  output [3:0] Chain_Out
);

  wire [1:0] bit_extender_1_out;
  wire [2:0] multiplexer_1_out;
  wire [9:0] shifter_1_out;

  Pull_Resistor pull_resistor_1 (.node(Control_In[1]));
  Pull_Resistor pull_resistor_2 (.node(Control_In[2]));
  Pull_Resistor pull_resistor_3 (.node(Control_In[3]));
  Pull_Resistor #(.pull(1)) pull_resistor_4 (.node(Control_In[0]));
  Multiplexer #(.select(2), .width(3), .disabled(0), .enable("false")) multiplexer_1 (
    .in0(3'b000), .in1({2'b00, Chain_In[0]}), .in2({1'b0, Chain_In[2:1]}), .in3(Chain_In[2:0]),
    .out(multiplexer_1_out), .sel(bit_extender_1_out));
  Bit_Extender #(.in_width(4), .out_width(2)) bit_extender_1 (.in(Control_In), .out(bit_extender_1_out));
  Shifter #(.width(10), .shift("lr")) shifter_1 (
    .in({multiplexer_1_out, Data_In, 3'b000}), .\dist (Control_In),
    .out({shifter_1_out[9:7], Data_Out, shifter_1_out[2:0]}));
  Multiplexer #(.select(2), .width(4), .disabled(0), .enable("false")) multiplexer_2 (
    .in0({1'b0, Data_Out[1:0], Data_Out[0]}), .in1({1'b0, Data_Out[1:0], shifter_1_out[2]}),
    .in2({1'b0, shifter_1_out[2:1], shifter_1_out[1]}), .in3({1'b0, shifter_1_out[2:0]}), .out(Chain_Out),
    .sel(bit_extender_1_out));

  assign Control_Out = Control_In;
  assign out_4 = Data_Out[3];
  assign out_5 = Data_Out[2];
  assign out_6 = Data_Out[1];
  assign out_7 = Data_Out[0];

  // Notes on the sheet:
  //   Chain_In: pull=down
  //   Data_In: pull=down
endmodule

module Splitter (
  input  [3:0] _4_Bit_Port_A___dcba,
  input  [3:0] _2_Bit_Port_B___xxdc,
  output [3:0] Port_a___xxba,
  output [3:0] Port_b___xxxb,
  output [3:0] Port_c___xxdc,
  output [3:0] Port_d___xxxd
);


  assign _4_Bit_Port_A___dcba[3:2] = _2_Bit_Port_B___xxdc[1:0];
  assign Port_a___xxba[1:0] = _4_Bit_Port_A___dcba[1:0];
  assign Port_b___xxxb[0] = _4_Bit_Port_A___dcba[1];
  assign Port_c___xxdc[1:0] = _2_Bit_Port_B___xxdc[1:0];
  assign Port_d___xxxd[0] = _2_Bit_Port_B___xxdc[1];
endmodule
